# Fritzing sketch etsen_glas_hightech (saved by Fritzing 0.9.3b)

parts:
  Onderdeel1 = Arduino Nano (Rev3.0)
  LED1 = prefix0000
  R1 = Photocell (LDR) [package=THT]
  R2 = Resistor [tolerance=±5% resistance=16k package=THT]
  RHT1 = Humidity and Temperature Sensor RHT03

nets:
  N1: Onderdeel1.D2, LED1.connector2
  N2: Onderdeel1.D8, RHT1.Data-signal
  N3: Onderdeel1.GND, LED1.connector3, R1.pin_0, RHT1.GND_2
  5V: Onderdeel1.5V, LED1.connector1, R2.Pin_1, RHT1.Vcc
  N4: Onderdeel1.A0, R1.pin_1, R2.Pin_0
